# Fritzing sketch led demo (saved by Fritzing 0.9.3b)
breadboards: 1

parts:
  Part1 = Arduino Nano (Rev3.0)
  LED1 = smd LED [color="Red (633nm)" package="1206 [SMD]"]
  LED2 = smd LED [color="Red (633nm)" package="1206 [SMD]"]
  LED3 = smd LED [color="Red (633nm)" package="1206 [SMD]"]
  LED4 = smd LED [color="Red (633nm)" package="1206 [SMD]"]
  LED5 = smd LED [color="Red (633nm)" package="1206 [SMD]"]
  LED6 = smd LED [color="Red (633nm)" package="1206 [SMD]"]
  LED7 = smd LED [color="Red (633nm)" package="1206 [SMD]"]
  LED8 = smd LED [color="Red (633nm)" package="1206 [SMD]"]
  LED9 = smd LED [color="Red (633nm)" package="1206 [SMD]"]
  LED10 = smd LED [color="Red (633nm)" package="1206 [SMD]"]
  Part2 = Bluetooth HC-05 Macho

nets:
  N1: Part1.D1/TX, Part2.RXD
  N2: Part1.D0/RX, Part2.TXD
  GND: Part1.GND, LED1.cathode, LED2.cathode, LED3.cathode, LED4.cathode, LED5.cathode, LED6.cathode, LED7.cathode, LED8.cathode, LED9.cathode, LED10.cathode, Part2.GND
  N3: Part1.D3, LED2.anode
  N4: Part1.D4, LED3.anode
  N5: Part1.D5, LED4.anode
  N6: Part1.D6, LED5.anode
  N7: Part1.D7, LED6.anode
  N8: Part1.D8, LED7.anode
  N9: Part1.D9, LED8.anode
  N10: Part1.D10, LED9.anode
  N11: Part1.D11/MOSI, LED10.anode
  N12: Part1.D12/MISO, LED1.anode
  5V: Part1.5V, Part2.VCC
